# Fritzing sketch LED_Schematic (saved by Fritzing 0.9.3b)
breadboards: 1

parts:
  LED1 = RGB LED (com. cathode, rgb) [package="5 mm [THT]"]
  LED2 = RGB LED (com. cathode, rgb) [package="5 mm [THT]"]
  パーツ2 = Arduino Pro Mini (3.3V)
  LED3 = RGB LED (com. cathode, rgb) [package="5 mm [THT]"]
  LED4 = RGB LED (com. cathode, rgb) [package="5 mm [THT]"]
  LED5 = RGB LED (com. cathode, rgb) [package="5 mm [THT]"]
  LED6 = RGB LED (com. cathode, rgb) [package="5 mm [THT]"]
  LED7 = RGB LED (com. cathode, rgb) [package="5 mm [THT]"]
  LED8 = RGB LED (com. cathode, rgb) [package="5 mm [THT]"]
  LED9 = RGB LED (com. cathode, rgb) [package="5 mm [THT]"]
  VCC1 = Battery

nets:
  N1: LED1.red_anode, LED2.red_anode, パーツ2.D10, LED3.red_anode, LED4.red_anode, LED5.red_anode, LED6.red_anode, LED7.red_anode, LED8.red_anode, LED9.red_anode
  N2: LED1.common_cathode, LED2.common_cathode, パーツ2.MOSI, LED3.common_cathode, LED4.common_cathode, LED5.common_cathode, LED6.common_cathode, LED7.common_cathode, LED8.common_cathode, LED9.common_cathode
  N3: LED1.green_anode, パーツ2.TXO
  N4: LED1.blue_anode, LED2.blue_anode, パーツ2.D9, LED3.blue_anode, LED4.blue_anode, LED5.blue_anode, LED6.blue_anode, LED7.blue_anode, LED8.blue_anode, LED9.blue_anode
  N5: LED2.green_anode, パーツ2.RXI
  N6: パーツ2.VCC, VCC1.+
  N7: パーツ2.GND, VCC1.-
  N8: パーツ2.D8, LED9.green_anode
  N9: パーツ2.D7, LED8.green_anode
  N10: パーツ2.D6, LED7.green_anode
  N11: パーツ2.D5, LED6.green_anode
  N12: パーツ2.D4, LED5.green_anode
  N13: パーツ2.D3, LED4.green_anode
  N14: パーツ2.D2, LED3.green_anode
